// Logisim project snake.circ as structural Verilog: 2 circuits, main circuit main
module main (
  input  [3:0] in_1,
  input  [3:0] in_2,
  input  in_3,
  input  in_4
);

  wire clock_1_out;
  wire [15:0] data_to_screen_1_out_6, data_to_screen_1_out_7, data_to_screen_1_out_8, data_to_screen_1_out_9,
       data_to_screen_1_out_10, data_to_screen_1_out_11, data_to_screen_1_out_12, data_to_screen_1_out_13,
       data_to_screen_1_out_14, data_to_screen_1_out_15, data_to_screen_1_out_16, data_to_screen_1_out_17,
       data_to_screen_1_out_18, data_to_screen_1_out_19, data_to_screen_1_out_20, data_to_screen_1_out_21;

  Clock clock_1 (.out(clock_1_out));
  DotMatrix #(.inputtype("row"), .matrixcols(16), .matrixrows(16)) dotmatrix_1 (
    .row0(data_to_screen_1_out_6), .row1(data_to_screen_1_out_7), .row2(data_to_screen_1_out_8),
    .row3(data_to_screen_1_out_9), .row4(data_to_screen_1_out_10), .row5(data_to_screen_1_out_11),
    .row6(data_to_screen_1_out_12), .row7(data_to_screen_1_out_13), .row8(data_to_screen_1_out_14),
    .row9(data_to_screen_1_out_15), .row10(data_to_screen_1_out_16), .row11(data_to_screen_1_out_17),
    .row12(data_to_screen_1_out_18), .row13(data_to_screen_1_out_19), .row14(data_to_screen_1_out_20),
    .row15(data_to_screen_1_out_21));
  data_to_screen data_to_screen_1 (
    .clock(clock_1_out), .X(in_1), .Y(in_2), .Value(in_3), .Stop(in_4), .out_6(data_to_screen_1_out_6),
    .out_7(data_to_screen_1_out_7), .out_8(data_to_screen_1_out_8), .out_10(data_to_screen_1_out_10),
    .out_11(data_to_screen_1_out_11), .out_12(data_to_screen_1_out_12), .out_13(data_to_screen_1_out_13),
    .out_14(data_to_screen_1_out_14), .out_15(data_to_screen_1_out_15), .out_16(data_to_screen_1_out_16),
    .out_17(data_to_screen_1_out_17), .out_18(data_to_screen_1_out_18), .out_19(data_to_screen_1_out_19),
    .out_20(data_to_screen_1_out_20), .out_21(data_to_screen_1_out_21), .out_9(data_to_screen_1_out_9));
endmodule

module data_to_screen (
  input  clock,
  input  [3:0] X,
  input  [3:0] Y,
  input  Value,
  input  Stop,
  output [15:0] out_6,
  output [15:0] out_7,
  output [15:0] out_8,
  output [15:0] out_9,
  output [15:0] out_10,
  output [15:0] out_11,
  output [15:0] out_12,
  output [15:0] out_13,
  output [15:0] out_14,
  output [15:0] out_15,
  output [15:0] out_16,
  output [15:0] out_17,
  output [15:0] out_18,
  output [15:0] out_19,
  output [15:0] out_20,
  output [15:0] out_21
);

  wire comparator_1_eq, comparator_2_eq, comparator_3_eq, comparator_4_eq, comparator_5_eq, comparator_6_eq,
       comparator_7_eq, comparator_8_eq, comparator_9_eq, comparator_10_eq, comparator_11_eq,
       comparator_12_eq, comparator_13_eq, comparator_14_eq, comparator_15_eq, comparator_16_eq, not_2_out,
       not_3_out, not_4_out, not_5_out, not_6_out, not_7_out, not_8_out, not_9_out, not_10_out, not_11_out,
       not_12_out, not_13_out, not_14_out, not_15_out, not_16_out, not_17_out, or_18_out, or_19_out,
       or_20_out, or_21_out, or_22_out, or_23_out, or_24_out, or_25_out, or_26_out, or_27_out, or_28_out,
       or_29_out, or_30_out, or_31_out, or_32_out, or_33_out;
  wire [15:0] and_2_out, and_3_out, and_4_out, and_5_out, and_6_out, and_7_out, and_8_out, and_9_out,
       and_10_out, and_11_out, and_12_out, and_13_out, and_14_out, and_15_out, and_16_out, and_17_out,
       multiplexer_1_out, multiplexer_2_out, multiplexer_3_out, multiplexer_4_out, multiplexer_5_out,
       multiplexer_6_out, multiplexer_7_out, multiplexer_8_out, multiplexer_9_out, multiplexer_10_out,
       multiplexer_11_out, multiplexer_12_out, multiplexer_13_out, multiplexer_14_out, multiplexer_15_out,
       multiplexer_16_out, multiplexer_17_out, multiplexer_18_out, multiplexer_19_out, multiplexer_20_out,
       multiplexer_21_out, multiplexer_22_out, multiplexer_23_out, multiplexer_24_out, multiplexer_25_out,
       multiplexer_26_out, multiplexer_27_out, multiplexer_28_out, multiplexer_29_out, multiplexer_30_out,
       multiplexer_31_out, multiplexer_32_out, or_2_out, or_3_out, or_4_out, or_5_out, or_6_out, or_7_out,
       or_8_out, or_9_out, or_10_out, or_11_out, or_12_out, or_13_out, or_14_out, or_15_out, or_16_out,
       or_17_out, shifter_1_out, shifter_2_out, shifter_3_out, shifter_4_out, shifter_5_out, shifter_6_out,
       shifter_7_out, shifter_8_out, shifter_9_out, shifter_10_out, shifter_11_out, shifter_12_out,
       shifter_13_out, shifter_14_out, shifter_15_out, shifter_16_out;

  // AND_Gate and_1 is placed but not wired
  // NOT_Gate not_1 is placed but not wired
  Shifter #(.width(16), .shift("lr")) shifter_1 (.in(16'h8000), .\dist (X), .out(shifter_1_out));
  Shifter #(.width(16), .shift("lr")) shifter_2 (.in(16'h8000), .\dist (X), .out(shifter_2_out));
  Shifter #(.width(16), .shift("lr")) shifter_3 (.in(16'h8000), .\dist (X), .out(shifter_3_out));
  Shifter #(.width(16), .shift("lr")) shifter_4 (.in(16'h8000), .\dist (X), .out(shifter_4_out));
  Shifter #(.width(16), .shift("lr")) shifter_5 (.in(16'h8000), .\dist (X), .out(shifter_5_out));
  Shifter #(.width(16), .shift("lr")) shifter_6 (.in(16'h8000), .\dist (X), .out(shifter_6_out));
  Shifter #(.width(16), .shift("lr")) shifter_7 (.in(16'h8000), .\dist (X), .out(shifter_7_out));
  Shifter #(.width(16), .shift("lr")) shifter_8 (.in(16'h8000), .\dist (X), .out(shifter_8_out));
  Shifter #(.width(16), .shift("lr")) shifter_9 (.in(16'h8000), .\dist (X), .out(shifter_9_out));
  Shifter #(.width(16), .shift("lr")) shifter_10 (.in(16'h8000), .\dist (X), .out(shifter_10_out));
  Shifter #(.width(16), .shift("lr")) shifter_11 (.in(16'h8000), .\dist (X), .out(shifter_11_out));
  Shifter #(.width(16), .shift("lr")) shifter_12 (.in(16'h8000), .\dist (X), .out(shifter_12_out));
  Shifter #(.width(16), .shift("lr")) shifter_13 (.in(16'h8000), .\dist (X), .out(shifter_13_out));
  Shifter #(.width(16), .shift("lr")) shifter_14 (.in(16'h8000), .\dist (X), .out(shifter_14_out));
  Shifter #(.width(16), .shift("lr")) shifter_15 (.in(16'h8000), .\dist (X), .out(shifter_15_out));
  Shifter #(.width(16), .shift("lr")) shifter_16 (.in(16'h8000), .\dist (X), .out(shifter_16_out));
  // OR_Gate or_1 is placed but not wired
  assign and_2_out = ~shifter_1_out & out_6;  // AND_Gate and_2, 16 bits wide
  Multiplexer #(.width(16)) multiplexer_1 (
    .in0(and_2_out), .in1(or_2_out), .out(multiplexer_1_out), .sel(Value));  // open: en
  assign or_2_out = out_6 | shifter_1_out;  // OR_Gate or_2, 16 bits wide
  Comparator #(.width(4), .mode("unsigned")) comparator_1 (.a(Y), .b(4'b0000), .eq(comparator_1_eq));  // open: gt, lt
  not not_2 (not_2_out, comparator_1_eq);
  assign and_3_out = ~shifter_2_out & out_7;  // AND_Gate and_3, 16 bits wide
  Multiplexer #(.width(16)) multiplexer_2 (
    .in0(and_3_out), .in1(or_3_out), .out(multiplexer_2_out), .sel(Value));  // open: en
  assign or_3_out = out_7 | shifter_2_out;  // OR_Gate or_3, 16 bits wide
  not not_3 (not_3_out, comparator_2_eq);
  Comparator #(.width(4), .mode("unsigned")) comparator_2 (.a(Y), .b(4'b0001), .eq(comparator_2_eq));  // open: gt, lt
  assign and_4_out = ~shifter_3_out & out_8;  // AND_Gate and_4, 16 bits wide
  Multiplexer #(.width(16)) multiplexer_3 (
    .in0(and_4_out), .in1(or_4_out), .out(multiplexer_3_out), .sel(Value));  // open: en
  assign or_4_out = out_8 | shifter_3_out;  // OR_Gate or_4, 16 bits wide
  not not_4 (not_4_out, comparator_3_eq);
  Comparator #(.width(4), .mode("unsigned")) comparator_3 (.a(Y), .b(4'b0010), .eq(comparator_3_eq));  // open: gt, lt
  assign and_5_out = ~shifter_4_out & out_9;  // AND_Gate and_5, 16 bits wide
  Multiplexer #(.width(16)) multiplexer_4 (
    .in0(and_5_out), .in1(or_5_out), .out(multiplexer_4_out), .sel(Value));  // open: en
  assign or_5_out = out_9 | shifter_4_out;  // OR_Gate or_5, 16 bits wide
  Comparator #(.width(4), .mode("unsigned")) comparator_4 (.a(Y), .b(4'b0011), .eq(comparator_4_eq));  // open: gt, lt
  not not_5 (not_5_out, comparator_4_eq);
  assign and_6_out = ~shifter_5_out & out_10;  // AND_Gate and_6, 16 bits wide
  Multiplexer #(.width(16)) multiplexer_5 (
    .in0(and_6_out), .in1(or_6_out), .out(multiplexer_5_out), .sel(Value));  // open: en
  assign or_6_out = out_10 | shifter_5_out;  // OR_Gate or_6, 16 bits wide
  Comparator #(.width(4), .mode("unsigned")) comparator_5 (.a(Y), .b(4'b0100), .eq(comparator_5_eq));  // open: gt, lt
  not not_6 (not_6_out, comparator_5_eq);
  assign and_7_out = ~shifter_6_out & out_11;  // AND_Gate and_7, 16 bits wide
  Multiplexer #(.width(16)) multiplexer_6 (
    .in0(and_7_out), .in1(or_7_out), .out(multiplexer_6_out), .sel(Value));  // open: en
  assign or_7_out = out_11 | shifter_6_out;  // OR_Gate or_7, 16 bits wide
  Comparator #(.width(4), .mode("unsigned")) comparator_6 (.a(Y), .b(4'b0101), .eq(comparator_6_eq));  // open: gt, lt
  not not_7 (not_7_out, comparator_6_eq);
  assign and_8_out = ~shifter_7_out & out_12;  // AND_Gate and_8, 16 bits wide
  Multiplexer #(.width(16)) multiplexer_7 (
    .in0(and_8_out), .in1(or_8_out), .out(multiplexer_7_out), .sel(Value));  // open: en
  assign or_8_out = out_12 | shifter_7_out;  // OR_Gate or_8, 16 bits wide
  Comparator #(.width(4), .mode("unsigned")) comparator_7 (.a(Y), .b(4'b0110), .eq(comparator_7_eq));  // open: gt, lt
  not not_8 (not_8_out, comparator_7_eq);
  assign and_9_out = ~shifter_8_out & out_13;  // AND_Gate and_9, 16 bits wide
  Multiplexer #(.width(16)) multiplexer_8 (
    .in0(and_9_out), .in1(or_9_out), .out(multiplexer_8_out), .sel(Value));  // open: en
  assign or_9_out = out_13 | shifter_8_out;  // OR_Gate or_9, 16 bits wide
  Comparator #(.width(4), .mode("unsigned")) comparator_8 (.a(Y), .b(4'b0111), .eq(comparator_8_eq));  // open: gt, lt
  not not_9 (not_9_out, comparator_8_eq);
  assign and_10_out = ~shifter_9_out & out_14;  // AND_Gate and_10, 16 bits wide
  Multiplexer #(.width(16)) multiplexer_9 (
    .in0(and_10_out), .in1(or_10_out), .out(multiplexer_9_out), .sel(Value));  // open: en
  assign or_10_out = out_14 | shifter_9_out;  // OR_Gate or_10, 16 bits wide
  Comparator #(.width(4), .mode("unsigned")) comparator_9 (.a(Y), .b(4'b1000), .eq(comparator_9_eq));  // open: gt, lt
  not not_10 (not_10_out, comparator_9_eq);
  assign and_11_out = ~shifter_10_out & out_15;  // AND_Gate and_11, 16 bits wide
  Multiplexer #(.width(16)) multiplexer_10 (
    .in0(and_11_out), .in1(or_11_out), .out(multiplexer_10_out), .sel(Value));  // open: en
  assign or_11_out = out_15 | shifter_10_out;  // OR_Gate or_11, 16 bits wide
  Comparator #(.width(4), .mode("unsigned")) comparator_10 (.a(Y), .b(4'b1001), .eq(comparator_10_eq));  // open: gt, lt
  not not_11 (not_11_out, comparator_10_eq);
  assign and_12_out = ~shifter_11_out & out_16;  // AND_Gate and_12, 16 bits wide
  Multiplexer #(.width(16)) multiplexer_11 (
    .in0(and_12_out), .in1(or_12_out), .out(multiplexer_11_out), .sel(Value));  // open: en
  assign or_12_out = out_16 | shifter_11_out;  // OR_Gate or_12, 16 bits wide
  Comparator #(.width(4), .mode("unsigned")) comparator_11 (.a(Y), .b(4'b1010), .eq(comparator_11_eq));  // open: gt, lt
  not not_12 (not_12_out, comparator_11_eq);
  assign and_13_out = ~shifter_12_out & out_17;  // AND_Gate and_13, 16 bits wide
  Multiplexer #(.width(16)) multiplexer_12 (
    .in0(and_13_out), .in1(or_13_out), .out(multiplexer_12_out), .sel(Value));  // open: en
  assign or_13_out = out_17 | shifter_12_out;  // OR_Gate or_13, 16 bits wide
  Comparator #(.width(4), .mode("unsigned")) comparator_12 (.a(Y), .b(4'b1011), .eq(comparator_12_eq));  // open: gt, lt
  not not_13 (not_13_out, comparator_12_eq);
  assign and_14_out = ~shifter_13_out & out_18;  // AND_Gate and_14, 16 bits wide
  Multiplexer #(.width(16)) multiplexer_13 (
    .in0(and_14_out), .in1(or_14_out), .out(multiplexer_13_out), .sel(Value));  // open: en
  assign or_14_out = out_18 | shifter_13_out;  // OR_Gate or_14, 16 bits wide
  Comparator #(.width(4), .mode("unsigned")) comparator_13 (.a(Y), .b(4'b1100), .eq(comparator_13_eq));  // open: gt, lt
  not not_14 (not_14_out, comparator_13_eq);
  assign and_15_out = ~shifter_14_out & out_19;  // AND_Gate and_15, 16 bits wide
  Multiplexer #(.width(16)) multiplexer_14 (
    .in0(and_15_out), .in1(or_15_out), .out(multiplexer_14_out), .sel(Value));  // open: en
  assign or_15_out = out_19 | shifter_14_out;  // OR_Gate or_15, 16 bits wide
  Comparator #(.width(4), .mode("unsigned")) comparator_14 (.a(Y), .b(4'b1101), .eq(comparator_14_eq));  // open: gt, lt
  not not_15 (not_15_out, comparator_14_eq);
  assign and_16_out = ~shifter_15_out & out_20;  // AND_Gate and_16, 16 bits wide
  Multiplexer #(.width(16)) multiplexer_15 (
    .in0(and_16_out), .in1(or_16_out), .out(multiplexer_15_out), .sel(Value));  // open: en
  assign or_16_out = out_20 | shifter_15_out;  // OR_Gate or_16, 16 bits wide
  not not_16 (not_16_out, comparator_15_eq);
  Comparator #(.width(4), .mode("unsigned")) comparator_15 (.a(Y), .b(4'b1110), .eq(comparator_15_eq));  // open: gt, lt
  assign and_17_out = ~shifter_16_out & out_21;  // AND_Gate and_17, 16 bits wide
  Multiplexer #(.width(16)) multiplexer_16 (
    .in0(and_17_out), .in1(or_17_out), .out(multiplexer_16_out), .sel(Value));  // open: en
  assign or_17_out = out_21 | shifter_16_out;  // OR_Gate or_17, 16 bits wide
  Comparator #(.width(4), .mode("unsigned")) comparator_16 (.a(Y), .b(4'b1111), .eq(comparator_16_eq));  // open: gt, lt
  not not_17 (not_17_out, comparator_16_eq);
  or or_18 (or_18_out, Stop, not_2_out);
  or or_19 (or_19_out, Stop, not_3_out);
  or or_20 (or_20_out, Stop, not_4_out);
  Multiplexer #(.width(16)) multiplexer_17 (
    .in0(multiplexer_4_out), .in1(out_9), .out(multiplexer_17_out), .sel(or_21_out));  // open: en
  or or_21 (or_21_out, Stop, not_5_out);
  Multiplexer #(.width(16)) multiplexer_18 (
    .in0(multiplexer_5_out), .in1(out_10), .out(multiplexer_18_out), .sel(or_22_out));  // open: en
  or or_22 (or_22_out, Stop, not_6_out);
  Multiplexer #(.width(16)) multiplexer_19 (
    .in0(multiplexer_6_out), .in1(out_11), .out(multiplexer_19_out), .sel(or_23_out));  // open: en
  or or_23 (or_23_out, Stop, not_7_out);
  Multiplexer #(.width(16)) multiplexer_20 (
    .in0(multiplexer_7_out), .in1(out_12), .out(multiplexer_20_out), .sel(or_24_out));  // open: en
  or or_24 (or_24_out, Stop, not_8_out);
  Multiplexer #(.width(16)) multiplexer_21 (
    .in0(multiplexer_8_out), .in1(out_13), .out(multiplexer_21_out), .sel(or_25_out));  // open: en
  or or_25 (or_25_out, Stop, not_9_out);
  Multiplexer #(.width(16)) multiplexer_22 (
    .in0(multiplexer_9_out), .in1(out_14), .out(multiplexer_22_out), .sel(or_26_out));  // open: en
  or or_26 (or_26_out, Stop, not_10_out);
  Multiplexer #(.width(16)) multiplexer_23 (
    .in0(multiplexer_10_out), .in1(out_15), .out(multiplexer_23_out), .sel(or_27_out));  // open: en
  or or_27 (or_27_out, Stop, not_11_out);
  Multiplexer #(.width(16)) multiplexer_24 (
    .in0(multiplexer_11_out), .in1(out_16), .out(multiplexer_24_out), .sel(or_28_out));  // open: en
  or or_28 (or_28_out, Stop, not_12_out);
  Multiplexer #(.width(16)) multiplexer_25 (
    .in0(multiplexer_12_out), .in1(out_17), .out(multiplexer_25_out), .sel(or_29_out));  // open: en
  or or_29 (or_29_out, Stop, not_13_out);
  Multiplexer #(.width(16)) multiplexer_26 (
    .in0(multiplexer_13_out), .in1(out_18), .out(multiplexer_26_out), .sel(or_30_out));  // open: en
  or or_30 (or_30_out, Stop, not_14_out);
  Multiplexer #(.width(16)) multiplexer_27 (
    .in0(multiplexer_14_out), .in1(out_19), .out(multiplexer_27_out), .sel(or_31_out));  // open: en
  or or_31 (or_31_out, Stop, not_15_out);
  Multiplexer #(.width(16)) multiplexer_28 (
    .in0(multiplexer_15_out), .in1(out_20), .out(multiplexer_28_out), .sel(or_32_out));  // open: en
  or or_32 (or_32_out, Stop, not_16_out);
  Multiplexer #(.width(16)) multiplexer_29 (
    .in0(multiplexer_16_out), .in1(out_21), .out(multiplexer_29_out), .sel(or_33_out));  // open: en
  or or_33 (or_33_out, Stop, not_17_out);
  Multiplexer #(.width(16)) multiplexer_30 (
    .in0(multiplexer_1_out), .in1(out_6), .out(multiplexer_30_out), .sel(or_18_out));  // open: en
  Register #(.width(16)) register_1 (.D(multiplexer_30_out), .Q(out_6), .clk(clock));  // open: en, clr
  Multiplexer #(.width(16)) multiplexer_31 (
    .in0(multiplexer_2_out), .in1(out_7), .out(multiplexer_31_out), .sel(or_19_out));  // open: en
  Register #(.width(16)) register_2 (.D(multiplexer_31_out), .Q(out_7), .clk(clock));  // open: en, clr
  Multiplexer #(.width(16)) multiplexer_32 (
    .in0(multiplexer_3_out), .in1(out_8), .out(multiplexer_32_out), .sel(or_20_out));  // open: en
  Register #(.width(16)) register_3 (.D(multiplexer_32_out), .Q(out_8), .clk(clock));  // open: en, clr
  Register #(.width(16)) register_4 (.D(multiplexer_17_out), .Q(out_9), .clk(clock));  // open: en, clr
  Register #(.width(16)) register_5 (.D(multiplexer_18_out), .Q(out_10), .clk(clock));  // open: en, clr
  Register #(.width(16)) register_6 (.D(multiplexer_19_out), .Q(out_11), .clk(clock));  // open: en, clr
  Register #(.width(16)) register_7 (.D(multiplexer_20_out), .Q(out_12), .clk(clock));  // open: en, clr
  Register #(.width(16)) register_8 (.D(multiplexer_21_out), .Q(out_13), .clk(clock));  // open: en, clr
  Register #(.width(16)) register_9 (.D(multiplexer_22_out), .Q(out_14), .clk(clock));  // open: en, clr
  Register #(.width(16)) register_10 (.D(multiplexer_23_out), .Q(out_15), .clk(clock));  // open: en, clr
  Register #(.width(16)) register_11 (.D(multiplexer_24_out), .Q(out_16), .clk(clock));  // open: en, clr
  Register #(.width(16)) register_12 (.D(multiplexer_25_out), .Q(out_17), .clk(clock));  // open: en, clr
  Register #(.width(16)) register_13 (.D(multiplexer_26_out), .Q(out_18), .clk(clock));  // open: en, clr
  Register #(.width(16)) register_14 (.D(multiplexer_27_out), .Q(out_19), .clk(clock));  // open: en, clr
  Register #(.width(16)) register_15 (.D(multiplexer_28_out), .Q(out_20), .clk(clock));  // open: en, clr
  Register #(.width(16)) register_16 (.D(multiplexer_29_out), .Q(out_21), .clk(clock));  // open: en, clr
endmodule
